# Fritzing sketch Schematics (saved by Fritzing 0.9.3b)
breadboards: 1

parts:
  Part1 = Arduino Uno (Rev3)
  KY-1 = Keyes Relay [package=THT]
  VCC1 = Battery block 9V
  Part2 = Soil Moisture Sensor
  M1 = DC Motor

nets:
  N1: Part1.A0, Part2.SIG
  N2: Part1.D8, KY-1.signal
  5V: Part1.5V, KY-1.power, Part2.VCC
  GND: Part1.GND, KY-1.ground, Part2.GND
  N3: KY-1.C, VCC1.+
  N4: KY-1.NO, M1.pin_2
  N5: VCC1.-, M1.pin_1

custom parts:
  Keyes Relay: The Keyes 5V relay module is suitable for SCM development, home appliance control. It uses a 5V~12V TIL control signal which can control DC / AC signal.
